# Fritzing sketch thermostat1 (saved by Fritzing 0.9.2b)
circuit board: 11.4441cm x 6.95677cm
breadboards: 1

parts:
  U1 = ESP8266 WiFi Module [part_number=ESP8266]
  U2 = PCF8574 [package="DIP16 [THT]"]
  Fan = Inductor [package="1206 [SMD]"]
  Compressor = Inductor [package="1206 [SMD]"]
  R6 = Resistor [tolerance=±5% resistance=220 package=THT]
  Reversing = Inductor [package="1206 [SMD]"]
  UP = Momentary Switch [package=tactile-pth]
  MENU = Momentary Switch [package=tactile-pth]
  DOWN = Momentary Switch [package=tactile-pth]
  Q1 = PNP-Transistor [package="TO92 [THT]"]
  R7 = Resistor [tolerance=±5% resistance=220 package=THT]
  TFT1 = 1.8" TFT Display with uSD
  R8 = Resistor [tolerance=±5% resistance=4.7k package=THT]
  DS1 = DS18B20 1-Wire Temperature Sensor [part_number=DS18B20]
  PIR1 = PIR sensor
  R3 = Resistor [tolerance=±5% resistance=220 package=THT]
  R2 = Resistor [tolerance=±5% resistance=220 package=THT]
  Q2 = PNP-Transistor [package="TO92 [THT]"]  # not connected
  U3 = RELAY [package=relay-g5q]  # not connected
  L1 = Inductor [package="0805 [SMD]"]  # not connected

nets:
  3.3V: U1.VCC, U1.CH_PD, U1.REST, U2.VCC, R6.Pin_0, Q1.E, TFT1.MISO, R8.Pin_0, DS1.VDD, PIR1.VDD, R3.Pin_0, R2.Pin_0
  N1: U1.GPIO_0, U2.SDA
  N2: U1.GPIO_2, U2.SCL
  GND: U1.GND, U2.A0, U2.A1, U2.A3, U2.GND, Fan.pin_1, Compressor.pin_1, Reversing.pin_1, UP.1, MENU.1, DOWN.1, TFT1.BL, DS1.GND, PIR1.GND
  N3: U1.GPIO_15, TFT1.SDCS
  N4: U1.GPIO_4, R8.Pin_1, DS1.DQ
  N5: U1.GPIO_5, TFT1.MOSI
  N6: U1.GPIO_14, TFT1.RST
  N7: U1.GPIO_13, TFT1.D/C
  N8: U2.P0, UP.3
  N9: U2.P1, MENU.3
  N10: U2.P2, DOWN.3
  N11: U2.P6, R7.Pin_0
  N12: U2.P7, PIR1.SIG
  N13: Q1.B, R7.Pin_1
  N14: Q1.C, TFT1.GND

custom parts:
  ESP8266 WiFi Module: Generic WiFi Module based on the ESP8266 with onboard PCB antenna and UART communications
  1.8" TFT Display with uSD: 1.8" TFT Display with SPI control and MicroSD card
