# Fritzing sketch thermostat2-pcb (saved by Fritzing 0.9.2b)
circuit board: 4.90508cm x 3.85922cm
breadboards: 1

parts:
  J1 = female pin header, 8 pins [form="♀ (female)"]  # not connected
  J2 = female pin header, 8 pins [form="♀ (female)"]  # not connected
  IC4 = IC, DIP package, 16 pins [chip_label=IC]
  R3 = Resistor [tolerance=±5% resistance=220 package=THT]
  Q2 = NPN-Transistor [package="TO92 [THT]"]
  J4 = female pin header, 4 pins [form="♀ (female)"]
  J3 = screw terminal, 6 pins  # not connected
  R4 = Resistor [tolerance=±5% resistance=220 package=THT]
  R5 = Resistor [tolerance=±5% resistance=220 package=THT]
  R6 = Resistor [tolerance=±5% resistance=220 package=THT]
  R7 = Resistor [tolerance=±5% resistance=220 package=THT]
  R8 = Resistor [tolerance=±5% resistance=220 package=THT]
  R9 = Resistor [tolerance=±5% resistance=220 package=THT]
  Q4 = NPN-Transistor [package="TO92 [THT]"]
  Q5 = NPN-Transistor [package="TO92 [THT]"]
  Q6 = NPN-Transistor [package="TO92 [THT]"]
  R10 = Resistor [tolerance=±5% resistance=220 package=THT]
  J5 = female pin header, 5 pins [form="♀ (female)"]  # not connected
  J6 = female pin header, 3 pins [form="♀ (female)"]
  J7 = female pin header, 3 pins [form="♀ (female)"]  # not connected
  J8 = female pin header, 4 pins [form="♀ (female)"]  # not connected
  R11 = Resistor [tolerance=±5% resistance=220 package=THT]
  J9 = female pin header, 8 pins [form="♀ (female)"]  # not connected
  J10 = female pin header, 2 pins [form="♀ (female)"]  # not connected
  J11 = female pin header, 4 pins [form="♀ (female)"]
  J12 = female pin header, 2 pins [form="♀ (female)"]  # not connected
  IC1 = IC, DIP package, 6 pins [chip_label=IC]
  IC6 = IC, DIP package, 6 pins [chip_label=IC]
  IC5 = IC, DIP package, 6 pins [chip_label=IC]

nets:
  N1: IC4.pin1, IC4.pin2, IC4.pin3, IC4.pin8
  N2: IC4.pin7, IC1.pin2
  N3: IC4.pin9, IC5.pin2
  N4: R3.Pin_0, Q5.C
  N5: Q2.E, Q4.E, Q5.E, J6.pin2, R11.Pin_0
  N6: Q2.C, R8.Pin_0
  N7: J4.pin1, J11.pin1
  N8: J4.pin2, R4.Pin_1, J11.pin2
  N9: J4.pin4, R4.Pin_0, R6.Pin_0, R9.Pin_0, R10.Pin_0, J11.pin4
  N10: R5.Pin_0, Q6.C
  N11: R7.Pin_0, Q4.C
  N12: IC1.pin6, IC6.pin6, IC5.pin6
