# Fritzing sketch thermostat2 (saved by Fritzing 0.9.2b)
circuit board: 11.4441cm x 6.95677cm
breadboards: 1

parts:
  U1 = ESP8266 WiFi Module [part_number=ESP8266]
  U2 = PCF8574 [package="DIP16 [THT]"]
  U3 = MOC3031-M [package=dil06]
  U6 = TRIAC [package=to-92]
  R1 = Resistor [tolerance=±5% resistance=1k package=THT]
  Fan = Inductor [package="1206 [SMD]"]
  U7 = MOC3031-M [package=dil06]
  U8 = TRIAC [package=to-92]
  R4 = Resistor [tolerance=±5% resistance=1k package=THT]
  Compressor = Inductor [package="1206 [SMD]"]
  U10 = TRIAC [package=to-92]
  R5 = Resistor [tolerance=±5% resistance=1k package=THT]
  R6 = Resistor [tolerance=±5% resistance=470 package=THT]
  Reversing = Inductor [package="1206 [SMD]"]
  UP = Momentary Switch [package=tactile-pth]
  MENU = Momentary Switch [package=tactile-pth]
  DOWN = Momentary Switch [package=tactile-pth]
  Q1 = PNP-Transistor [package="TO92 [THT]"]
  R7 = Resistor [tolerance=±5% resistance=1k package=THT]
  TFT1 = 1.8" TFT Display with uSD
  R8 = Resistor [tolerance=±5% resistance=4.7k package=THT]
  DS1 = DS18B20 1-Wire Temperature Sensor [part_number=DS18B20]
  PIR1 = PIR sensor
  U9 = MOC3031-M [package=dil06]
  R3 = Resistor [tolerance=±5% resistance=470 package=THT]
  R2 = Resistor [tolerance=±5% resistance=470 package=THT]

nets:
  3.3V: U1.VCC, U1.CH_PD, U1.REST, U2.VCC, R6.Pin_0, Q1.E, TFT1.MISO, R8.Pin_0, DS1.VDD, PIR1.VDD, R3.Pin_0, R2.Pin_0
  N1: U1.GPIO_0, U2.SDA
  N2: U1.GPIO_2, U2.SCL
  GND: U1.GND, U2.A0, U2.A1, U2.A3, U2.GND, Fan.pin_1, Compressor.pin_1, Reversing.pin_1, UP.1, MENU.1, DOWN.1, TFT1.BL, DS1.GND, PIR1.GND
  N3: U1.GPIO_15, TFT1.SDCS
  N4: U1.GPIO_4, R8.Pin_1, DS1.DQ
  N5: U1.GPIO_5, TFT1.MOSI
  N6: U1.GPIO_14, TFT1.RST
  N7: U1.GPIO_13, TFT1.D/C
  N8: U2.P0, UP.3
  N9: U2.P1, MENU.3
  N10: U2.P2, DOWN.3
  N11: U2.P3, U9.2
  N12: U2.P4, U7.2
  N13: U2.P5, U3.2
  N14: U2.P6, R7.Pin_0
  N15: U2.P7, PIR1.SIG
  N16: U3.1, R2.Pin_1
  N17: U3.4, R1.Pin_0
  24V: U3.6, U6.M2, U7.6, U8.M2, U10.M2, U9.6
  N18: U6.M1, Fan.pin_0
  N19: U6.G, R1.Pin_1
  N20: U7.1, R3.Pin_1
  N21: U7.4, R4.Pin_0
  N22: U8.M1, Compressor.pin_0
  N23: U8.G, R4.Pin_1
  N24: U10.M1, Reversing.pin_0
  N25: U10.G, R5.Pin_1
  N26: R5.Pin_0, U9.4
  N27: R6.Pin_1, U9.1
  N28: Q1.B, R7.Pin_1
  N29: Q1.C, TFT1.GND

custom parts:
  ESP8266 WiFi Module: Generic WiFi Module based on the ESP8266 with onboard PCB antenna and UART communications
  1.8" TFT Display with uSD: 1.8" TFT Display with SPI control and MicroSD card
